# Fritzing sketch Gimbal MPU 6050 Test (saved by Fritzing 0.9.3b)

parts:
  GY1 = MPU-6050 Board GY-521 [form="♀ (female)" package=THT]
  Nano = Arduino Nano (Rev3.0) (ICSP)
  VCC1 = 4 x AAA Battery Mount
  J1 = Basic Servo
  J2 = Basic Servo
  J3 = Basic Servo

nets:
  N1: GY1.pin1, Nano.5V
  N2: GY1.pin2, Nano.GND, VCC1.-
  N3: GY1.pin3, Nano.A5
  N4: GY1.pin4, Nano.A4
  N5: GY1.pin8, Nano.D2
  N6: Nano.D8, J3.pulse
  N7: Nano.D9, J2.pulse
  N8: Nano.D10, J1.pulse
  N9: Nano.VIN, VCC1.+

notes:
  Yaw Servo
  Roll Servo
  Pitch Servo

custom parts:
  MPU-6050 Board GY-521: Acelerometro y Giroscopio MPU-6050 Board GY-521
