# Fritzing sketch MPU 6050 Test (saved by Fritzing 0.9.3b)

parts:
  GY1 = MPU-6050 Board GY-521 [form="♀ (female)" package=THT]
  Nano = Arduino Nano (Rev3.0) (ICSP)

nets:
  N1: GY1.pin1, Nano.5V
  N2: GY1.pin2, Nano.GND
  N3: GY1.pin3, Nano.A5
  N4: GY1.pin4, Nano.A4
  N5: GY1.pin8, Nano.D2

custom parts:
  MPU-6050 Board GY-521: Acelerometro y Giroscopio MPU-6050 Board GY-521
